# Fritzing sketch Mintduino Game Circuit Diagram (saved by Fritzing 0.7.12b)
breadboards: 2

parts:
  U1 = atmega168 [package=dip]
  S1 = Pushbutton [package="[THT]"]
  S2 = Pushbutton [package="[THT]"]
  LED1 = LED - 5mm [color="Red (633nm)" package="5 mm [THT]"]
  R1 = Resistor [tolerance=±5% resistance=100 package=THT]
  R2 = Resistor [tolerance=±5% resistance=100 package=THT]
  R3 = Resistor [tolerance=±5% resistance=100 package=THT]
  LED4 = green LED - 5mm
  LED5 = green LED - 5mm

nets:
  N1: U1.D2, S2.Pin_3, S2.Pin_4, R3.Pin_1, LED4.cathode
  N2: U1.D3_(PWM), S1.Pin_3, S1.Pin_4, R2.Pin_1, LED5.cathode
  N3: U1.D5_(PWM), LED5.anode
  N4: U1.D6_(PWM), LED4.anode
  N5: U1.D7, LED1.cathode
  N6: S1.Pin_1, S1.Pin_2, S2.Pin_1, S2.Pin_2
  N7: LED1.anode, R1.Pin_1
  N8: R1.Pin_0, R2.Pin_0, R3.Pin_0

notes:
  Mintduino
